# Fritzing sketch rotary_dial_tester (saved by Fritzing 0.9.3b)
breadboards: 1

parts:
  Part1 = Arduino Uno (Rev3)
  U1 = mystery part, 3 pins [chip_label="Rotary Dila, Siemens standard"]
  LED1 = LED - 5mm [color="Yellow (595nm)" package="5 mm [THT]"]
  LED2 = LED - 5mm [color="Green (570nm)" package="5 mm [THT]"]
  R1 = Resistor [tolerance=±5% resistance=330 package=THT]
  R2 = Resistor [tolerance=±5% resistance=330 package=THT]

nets:
  N1: Part1.D2, U1.pin1, R1.Pin_1
  N2: Part1.D3_PWM, U1.pin2, R2.Pin_1
  N3: Part1.5V, U1.pin3
  N4: Part1.GND, LED1.cathode, LED2.cathode
  N5: LED1.anode, R2.Pin_0
  N6: LED2.anode, R1.Pin_0
